// Logisim project K213064_soft_tasks.circ as structural Verilog: 1 circuit, main circuit main
module main (
  input  S_prime,
  input  R_prime,
  input  in_3,
  input  in_4,
  input  D,
  input  Enable,
  input  in_7,
  input  J,
  input  in_9,
  input  K,
  input  in_11,
  input  D_2,
  output Q,
  output Q_prime,
  output out_15,
  output out_16,
  output Q_2,
  output Q_prime_2,
  output out_19,
  output Q_3,
  output Q_prime_3,
  output out_22,
  output Q_4,
  output Q_prime_4
);

  wire and_1_out, and_2_out, and_5_out, and_6_out, Clock_2_out, Clock_out, nand_1_out, nand_2_out, not_1_out,
       not_2_out, undriven;

  Clock Clock (.out(Clock_out));
  not not_1 (not_1_out, D);
  not not_2 (not_2_out, D_2);
  and and_1 (and_1_out, out_19, in_7, in_9);
  and and_2 (and_2_out, in_9, in_11, in_11);
  and and_3 (Q, S_prime, Q_prime);
  // AND_Gate and_4 has open pins: in0=Q, in1=R_prime, out=open
  nor nor_1 (out_15, in_3, out_16);
  nor nor_2 (out_16, out_15, in_4);
  and and_5 (and_5_out, not_1_out, Enable);
  and and_6 (and_6_out, Enable, D);
  nand nand_1 (nand_1_out, D_2, Clock_out);
  nand nand_2 (nand_2_out, Clock_out, not_2_out);
  nand nand_3 (Q_4, nand_1_out, Q_prime_4);
  nand nand_4 (Q_prime_4, Q_4, nand_2_out);
  nor nor_3 (Q_2, and_5_out, Q_prime_2);
  nor nor_4 (Q_prime_2, Q_2, and_6_out);
  nor nor_5 (out_19, out_22, and_1_out);
  nor nor_6 (out_22, out_19, and_2_out);
  Clock Clock_2 (.out(Clock_2_out));
  J_K_Flip_Flop j_k_ff_1 (.J(J), .clk(Clock_2_out), .K(undriven), .Q(Q_3), .Qn(Q_prime_3));  // open: preset, en, reset

  // Notes on the sheet:
  //   JK flip flop using logic gates
  //   D flipflop using logic gates
  //   SR latch using nand gates
  //   SR latch using nor gates
  //   D latch using logic gates
  //   Jk flipflop using circuit
endmodule
