// Logisim project project.circ as structural Verilog: 3 circuits, main circuit main
module main (
  input  in_1,
  input  in_2,
  input  in_3,
  input  in_4
);

  wire asd_1_a, asd_1_b, asd_1_c, asd_1_d, asd_1_e, asd_1_f, asd_1_g, decrypt_complete_1_a,
       decrypt_complete_1_b, decrypt_complete_1_c, decrypt_complete_1_d, decrypt_complete_1_e,
       decrypt_complete_1_f, decrypt_complete_1_g;

  asd asd_1 (
    .w(in_1), .x(in_2), .y(in_3), .z(in_4), .a(asd_1_a), .b(asd_1_b), .c(asd_1_c), .d(asd_1_d), .e(asd_1_e),
    .f(asd_1_f), .g(asd_1_g));
  _7_Segment_Display u_7_segment_display_1 (
    .g(asd_1_g), .f(asd_1_f), .a(asd_1_a), .b(asd_1_b), .e(asd_1_e), .d(asd_1_d), .c(asd_1_c));  // open: dp
  decrypt_complete decrypt_complete_1 (
    .a1(asd_1_a), .a2(asd_1_b), .a3(asd_1_c), .a4(asd_1_d), .a5(asd_1_e), .a6(asd_1_f), .a7(asd_1_g),
    .a(decrypt_complete_1_a), .b(decrypt_complete_1_b), .c(decrypt_complete_1_c), .d(decrypt_complete_1_d),
    .e(decrypt_complete_1_e), .f(decrypt_complete_1_f), .g(decrypt_complete_1_g));
  _7_Segment_Display u_7_segment_display_2 (
    .g(decrypt_complete_1_g), .f(decrypt_complete_1_f), .a(decrypt_complete_1_a), .b(decrypt_complete_1_b),
    .e(decrypt_complete_1_e), .d(decrypt_complete_1_d), .c(decrypt_complete_1_c));  // open: dp
endmodule

module asd (
  input  w,
  input  x,
  input  y,
  input  z,
  output a,
  output b,
  output c,
  output d,
  output e,
  output f,
  output g
);

  wire and_1_out, and_2_out, and_3_out, and_4_out, and_5_out, and_6_out, and_7_out, and_8_out, and_9_out,
       and_10_out, and_11_out, not_1_out, not_2_out, not_3_out, not_4_out, not_5_out, not_6_out, not_7_out,
       not_8_out, not_9_out, not_10_out, not_11_out, not_12_out, not_13_out, not_14_out, not_15_out,
       not_16_out, not_17_out, not_18_out, not_19_out;

  not not_1 (not_1_out, x);
  and and_1 (and_1_out, not_1_out, z);
  not not_2 (not_2_out, x);
  and and_2 (and_2_out, not_2_out, y);
  and and_3 (and_3_out, x, not_3_out);
  not not_3 (not_3_out, y);
  and and_4 (and_4_out, x, not_4_out);
  not not_4 (not_4_out, z);
  not not_5 (not_5_out, w);
  and and_5 (and_5_out, not_5_out, not_6_out);
  not not_6 (not_6_out, z);
  not not_7 (not_7_out, x);
  and and_6 (and_6_out, not_7_out, y);
  and and_7 (and_7_out, x, not_8_out);
  not not_8 (not_8_out, y);
  and and_8 (and_8_out, w, z);
  not not_9 (not_9_out, w);
  and and_9 (and_9_out, not_9_out, not_10_out);
  not not_10 (not_10_out, y);
  not not_11 (not_11_out, w);
  and and_10 (and_10_out, not_11_out, z);
  not not_12 (not_12_out, w);
  and and_11 (and_11_out, not_12_out, not_13_out);
  not not_13 (not_13_out, y);
  not not_14 (not_14_out, z);
  not not_15 (not_15_out, x);
  or or_1 (e, not_15_out, z, y);
  not not_16 (not_16_out, x);
  or or_2 (f, not_16_out, not_17_out, y);
  not not_17 (not_17_out, z);
  not not_18 (not_18_out, x);
  not not_19 (not_19_out, y);
  or or_3 (g, not_18_out, not_19_out, z);
  or or_4 (a, and_1_out, and_2_out, and_3_out, and_4_out, w);
  or or_5 (b, and_5_out, and_6_out, and_7_out, and_8_out);
  or or_6 (c, and_9_out, and_10_out, x);
  or or_7 (d, and_11_out, not_14_out, x);
endmodule

module decrypt_complete (
  input  a1,
  input  a2,
  input  a3,
  input  a4,
  input  a5,
  input  a6,
  input  a7,
  output a,
  output b,
  output c,
  output d,
  output e,
  output f,
  output g
);

  wire and_1_out, and_3_out, and_4_out, and_5_out, and_6_out, and_7_out, and_8_out, and_9_out, and_10_out,
       and_11_out, not_1_out, not_2_out, not_3_out, not_4_out, not_5_out, not_6_out, not_7_out, not_8_out,
       not_9_out, not_10_out, not_11_out, not_12_out, not_13_out, not_14_out;

  not not_1 (not_1_out, a1);
  not not_2 (not_2_out, a3);
  and and_1 (and_1_out, a2, a5, a7);
  and and_2 (b, a6, a7);
  not not_3 (not_3_out, a2);
  not not_4 (not_4_out, a4);
  not not_5 (not_5_out, a2);
  not not_6 (not_6_out, a3);
  not not_7 (not_7_out, a4);
  not not_8 (not_8_out, a2);
  not not_9 (not_9_out, a3);
  not not_10 (not_10_out, a2);
  not not_11 (not_11_out, a3);
  not not_12 (not_12_out, a3);
  not not_13 (not_13_out, a4);
  not not_14 (not_14_out, a3);
  and and_3 (and_3_out, a1, a2);
  or or_1 (a, not_1_out, not_2_out, and_1_out);
  or or_2 (c, not_3_out, not_4_out, a3);
  and and_4 (and_4_out, not_5_out, not_6_out);
  and and_5 (and_5_out, a3, not_7_out);
  and and_6 (and_6_out, a2, a4, a5);
  and and_7 (and_7_out, not_8_out, not_9_out);
  and and_8 (and_8_out, a2, a4, a5, a6);
  and and_9 (and_9_out, not_10_out, not_11_out);
  and and_10 (and_10_out, not_12_out, not_13_out);
  and and_11 (and_11_out, a2, a3, a4);
  or or_3 (g, not_14_out, and_3_out);
  or or_4 (d, and_4_out, and_5_out, and_6_out);
  or or_5 (e, and_7_out, and_8_out);
  or or_6 (f, and_9_out, and_10_out, and_11_out);
endmodule
